# Fritzing sketch Arduino_BT_Setup (saved by Fritzing 0.9.3b)
breadboards: 1

parts:
  Part1 = Arduino Uno (Rev3)
  Part2 = Bluetooth HC-05 Macho
  C1 = Capacitor Polarized [package=panasonic_c]

nets:
  N1: Part1.D10_PWM/SS, Part2.TXD
  N2: Part1.D11_PWM/MOSI, Part2.RXD
  N3: Part1.RESET, C1.+
  5V: Part1.5V, Part2.VCC
  GND: Part1.GND, Part2.GND
  N4: Part2.State, C1.-
